# Fritzing sketch New Setup_lilygo ttgo (saved by Fritzing 0.9.3b)

parts:
  U1 = ESP32S-HiLetgo [part_number=ESP32S-HiLetgo]
  8_Channel_Relay1 = 8 Channel Power Relay
  JP1 = Header 6 [package=molex-1x6_lock]
  J1 = Generic male header - 4 pins [form="♂ (male)" package=THT]
  ANT1 = Antenna  # not connected
  Part1 = Bluetooth HC-05 Macho
  DS1 = DS18B20 1-Wire Temperature Sensor [part_number=DS18B20]
  ZS-042_RTC1 = ZS-042 RTC Module
  Part2 = SRF05 Ultrasonic Rangefinder
  DHT1 = DHT11 Humitidy and Temperature Sensor
  S1 = PH meter [package=THT]

nets:
  N1: U1.EN, Part1.TXD
  N2: U1.GPIO36, Part1.RXD
  N3: U1.GPIO39, DHT1.DATA
  N4: U1.GPIO35, 8_Channel_Relay1.IN3
  N5: U1.GPIO32, Part2.Echo
  N6: U1.GPIO33, Part2.Trig
  N7: U1.GPIO25, 8_Channel_Relay1.IN4
  N8: U1.GPIO27, ZS-042_RTC1.SCL
  N9: U1.GPIO14, 8_Channel_Relay1.IN6
  VCC: U1.GPIO11, 8_Channel_Relay1.VCC, DS1.VDD, ZS-042_RTC1.VCC, DHT1.VDD
  N10: U1.GPIO6, DHT1.GND
  N11: U1.GPIO15, JP1.3
  N12: U1.GPIO4, S1.pin1
  N13: U1.GPIO16, J1.PWM
  N14: U1.GPIO17, J1.Z-C
  N15: U1.GPIO19, 8_Channel_Relay1.IN2
  N16: U1.GPIO21, 8_Channel_Relay1.IN5
  N17: U1.GPIO3, DS1.DQ
  N18: U1.GPIO22, 8_Channel_Relay1.IN1
  N19: U1.GPIO23, ZS-042_RTC1.SDA
  GND: 8_Channel_Relay1.GND, ZS-042_RTC1.GND
  N20: JP1.5, DS1.GND, S1.pin3
  N21: JP1.6, S1.pin2
  VCC_2: J1.VCC, Part2.VCC
  GND_2: Part1.GND, Part2.GND

notes:
  pH Sensor 6 Pin
  TO
  DO
  PO
  GND
  GND
  VCC
  Keystone TDS Meter

custom parts:
  ESP32S-HiLetgo: HiLetgo ESP-WROOM-32 ESP32 ESP-32S Development Board 2.4GHz Dual-Mode WiFi + Bluetooth Dual Cores Microcontroller The ESP32 integrated with Antenna switches, RF Balun, power amplifiers, low-noise amplifiers, filters, and management modules, and the entire solution occupies the least area of PCB. 2.4 GHz Wi-Fi plus Bluetooth dual-mode chip, with TSMC Ultra-low power consumption 40nm technology,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
  8 Channel Power Relay: An 8 channel power relay. The module operates at 5V.
  Generic male header - 4 pins: Generic male header
  DHT11 Humitidy and Temperature Sensor: DHT11 Humidity and Temperature Sensor
